# Fritzing sketch Arduino mega + module 16 relays (saved by Fritzing 0.9.3b)
breadboards: 1

parts:
  K1 = Relay [part_number=FRS1B-S package=THT]  # not connected
  K2 = Relay [part_number=FRS1B-S package=THT]
  K3 = Relay [part_number=FRS1B-S package=THT]
  K4 = Relay [part_number=FRS1B-S package=THT]  # not connected
  K5 = Relay [part_number=FRS1B-S package=THT]
  K6 = Relay [part_number=FRS1B-S package=THT]
  K9 = Relay [part_number=FRS1B-S package=THT]
  K10 = Relay [part_number=FRS1B-S package=THT]
  Composant1 = Arduino Mega 2560 (Rev3)
  K17 = Relay [part_number=FRS1B-S package=THT]
  K18 = Relay [part_number=FRS1B-S package=THT]
  K19 = Relay [part_number=FRS1B-S package=THT]
  K20 = Relay [part_number=FRS1B-S package=THT]
  K21 = Relay [part_number=FRS1B-S package=THT]
  K22 = Relay [part_number=FRS1B-S package=THT]
  K23 = Relay [part_number=FRS1B-S package=THT]
  K24 = Relay [part_number=FRS1B-S package=THT]  # not connected

nets:
  N1: K2.C1, K2.C2, Composant1.D23
  N2: K3.C1, K3.C2, Composant1.D24
  N3: K5.A, K5.B
  N4: K6.C1, K6.C2, Composant1.D27
  N5: K9.COIL1, K9.COIL2
  N6: K9.C1, K9.C2, Composant1.D30
  N7: K10.C1, K10.C2, Composant1.D31
  N8: Composant1.D28, K17.C1, K17.C2
  N9: Composant1.D29, K18.C1, K18.C2
  N10: Composant1.D32, K19.C1, K19.C2
  N11: Composant1.D33, K20.C1, K20.C2
  N12: Composant1.D34, K21.C1, K21.C2
  N13: Composant1.D35, K22.C1, K22.C2
  N14: Composant1.D36, K23.C1, K23.C2
  N15: K18.A, K18.B
